# Fritzing sketch Sensor CO2 y Temperatura (saved by Fritzing 0.9.6b)

parts:
  U1 = NodeMCU V1.0
  TD-er1 = MH-Z19 CO2 sensor [part_number=MH-Z19]

nets:
  N1: U1.RX, TD-er1.TX
  N2: U1.TX, TD-er1.RX
  GND: U1.GND, TD-er1.GND
  VIN: U1.Vin, TD-er1.Vin

custom parts:
  NodeMCU V1.0: ESP8266 based NodeMCU
